// Logisim project 7SegmentHexDec.circ as structural Verilog: 1 circuit, main circuit main
module main (
);

  wire n7404_1_pin2, n7404_1_pin7, n7404_1_pin8, n7404_1_pin10, n7404_1_pin12, n7404_1_pin14, n7408_1_pin3,
       n7408_1_pin6, n7408_1_pin8, n7408_1_pin11, n7408_2_pin8, n7408_2_pin11, n7408_3_pin11, n7408_4_pin3,
       n7408_4_pin6, n7408_4_pin8, n7408_4_pin9, n7408_4_pin11, n7408_4_pin12, n7408_5_pin3, n7408_5_pin6,
       n7408_5_pin8, n7408_5_pin11, n7408_6_pin3, n7408_6_pin6, n7408_6_pin8, n7408_6_pin11, n7408_7_pin3,
       n7408_7_pin6, n7408_7_pin8, n7408_7_pin11, n7408_8_pin3, n7408_8_pin6, n7408_8_pin8, n7408_8_pin11,
       n7411_1_pin6, n7411_1_pin12, n7411_2_pin6, n7411_2_pin8, n7411_2_pin12, n7411_3_pin12, n7432_1_pin2,
       n7432_1_pin6, n7432_1_pin11, n7432_2_pin3, n7432_2_pin6, n7432_2_pin11, n7432_2_pin12, n7432_3_pin1,
       n7432_3_pin2, n7432_3_pin3, n7432_3_pin5, n7432_3_pin6, n7432_3_pin8, n7432_3_pin11, n7432_4_pin3,
       n7432_5_pin3, n7432_5_pin6, n7432_5_pin8, n7432_5_pin11, n7432_6_pin3, n7432_6_pin8, n7432_6_pin11,
       n7432_7_pin3, n7432_7_pin5, n7432_7_pin6, n7432_7_pin11, n7432_8_pin3, n7432_8_pin6, n7432_8_pin8,
       n7432_8_pin11, n7432_9_pin11;
  wire [3:0] dipswitch_1_sw4;

  Hex_Digit_Display hex_digit_display_1 (.value(dipswitch_1_sw4));  // open: dp
  DipSwitch #(.number(4)) dipswitch_1 (
    .sw1(dipswitch_1_sw4[3]), .sw2(dipswitch_1_sw4[2]), .sw3(dipswitch_1_sw4[1]), .sw4(dipswitch_1_sw4[0]));
  _7404 #(.ShowInternalStructure("true"), .VccGndPorts("true")) u_7404_1 (
    .pin1(dipswitch_1_sw4[0]), .pin2(n7404_1_pin2), .pin7(n7404_1_pin7), .pin14(n7404_1_pin14),
    .pin13(dipswitch_1_sw4[3]), .pin12(n7404_1_pin12), .pin11(dipswitch_1_sw4[2]), .pin10(n7404_1_pin10),
    .pin9(dipswitch_1_sw4[1]), .pin8(n7404_1_pin8));  // open: pin3, pin4, pin5, pin6
  _7411 #(.ShowInternalStructure("true"), .VccGndPorts("true")) u_7411_1 (
    .pin1(n7404_1_pin10), .pin2(n7404_1_pin8), .pin3(n7404_1_pin12), .pin4(dipswitch_1_sw4[0]),
    .pin5(dipswitch_1_sw4[2]), .pin6(n7411_1_pin6), .pin7(n7404_1_pin7), .pin14(n7404_1_pin14),
    .pin13(dipswitch_1_sw4[3]), .pin12(n7411_1_pin12));  // open: pin11, pin10, pin9, pin8
  _7408 #(.ShowInternalStructure("true"), .VccGndPorts("true")) u_7408_1 (
    .pin1(n7404_1_pin12), .pin2(dipswitch_1_sw4[1]), .pin3(n7408_1_pin3), .pin4(dipswitch_1_sw4[3]),
    .pin5(n7404_1_pin2), .pin6(n7408_1_pin6), .pin7(n7404_1_pin7), .pin14(n7404_1_pin14),
    .pin13(n7404_1_pin12), .pin12(n7404_1_pin2), .pin11(n7408_1_pin11), .pin10(dipswitch_1_sw4[2]),
    .pin9(dipswitch_1_sw4[1]), .pin8(n7408_1_pin8));
  _7411 #(.ShowInternalStructure("true"), .VccGndPorts("true")) u_7411_2 (
    .pin1(n7404_1_pin8), .pin2(n7404_1_pin2), .pin3(n7404_1_pin12), .pin4(dipswitch_1_sw4[1]),
    .pin5(dipswitch_1_sw4[0]), .pin6(n7411_2_pin6), .pin7(n7404_1_pin7), .pin14(n7404_1_pin14),
    .pin13(n7404_1_pin12), .pin12(n7411_2_pin12), .pin11(dipswitch_1_sw4[3]), .pin10(n7404_1_pin8),
    .pin9(dipswitch_1_sw4[0]), .pin8(n7411_2_pin8));
  _7408 #(.ShowInternalStructure("true"), .VccGndPorts("true")) u_7408_2 (
    .pin7(n7404_1_pin7), .pin14(n7404_1_pin14), .pin13(n7404_1_pin10), .pin12(n7404_1_pin8),
    .pin11(n7408_2_pin11), .pin10(n7404_1_pin10), .pin9(n7404_1_pin2), .pin8(n7408_2_pin8));  // open: pin1, pin2, pin3, pin4, pin5, pin6
  _7408 #(.ShowInternalStructure("true"), .VccGndPorts("true")) u_7408_3 (
    .pin7(n7404_1_pin7), .pin14(n7404_1_pin14), .pin13(dipswitch_1_sw4[3]), .pin12(n7404_1_pin8),
    .pin11(n7408_3_pin11));  // open: pin1, pin2, pin3, pin4, pin5, pin6, pin10, pin9, pin8
  _7408 #(.ShowInternalStructure("true"), .VccGndPorts("true")) u_7408_4 (
    .pin1(dipswitch_1_sw4[2]), .pin2(n7404_1_pin8), .pin3(n7408_4_pin3), .pin4(dipswitch_1_sw4[1]),
    .pin5(n7404_1_pin2), .pin6(n7408_4_pin6), .pin7(n7404_1_pin7), .pin14(n7404_1_pin14),
    .pin13(dipswitch_1_sw4[3]), .pin12(n7408_4_pin12), .pin11(n7408_4_pin11), .pin10(n7404_1_pin12),
    .pin9(n7408_4_pin9), .pin8(n7408_4_pin8));
  _7432 #(.ShowInternalStructure("true"), .VccGndPorts("true")) u_7432_1 (
    .pin1(n7408_4_pin3), .pin2(n7432_1_pin2), .pin3(n7408_4_pin9), .pin4(n7408_4_pin8), .pin5(n7408_4_pin6),
    .pin6(n7432_1_pin6), .pin7(n7404_1_pin7), .pin14(n7404_1_pin14), .pin13(n7404_1_pin10),
    .pin12(dipswitch_1_sw4[0]), .pin11(n7432_1_pin11), .pin10(n7432_1_pin11), .pin9(dipswitch_1_sw4[1]),
    .pin8(n7408_4_pin12));
  _7408 #(.ShowInternalStructure("true"), .VccGndPorts("true")) u_7408_5 (
    .pin1(n7404_1_pin10), .pin2(dipswitch_1_sw4[1]), .pin3(n7408_5_pin3), .pin4(n7408_5_pin3),
    .pin5(dipswitch_1_sw4[0]), .pin6(n7408_5_pin6), .pin7(n7404_1_pin7), .pin14(n7404_1_pin14),
    .pin13(n7404_1_pin12), .pin12(n7404_1_pin10), .pin11(n7408_5_pin11), .pin10(n7408_5_pin11),
    .pin9(n7404_1_pin2), .pin8(n7408_5_pin8));
  _7408 #(.ShowInternalStructure("true"), .VccGndPorts("true")) u_7408_6 (
    .pin1(dipswitch_1_sw4[2]), .pin2(dipswitch_1_sw4[1]), .pin3(n7408_6_pin3), .pin4(n7408_6_pin3),
    .pin5(n7404_1_pin2), .pin6(n7408_6_pin6), .pin7(n7404_1_pin7), .pin14(n7404_1_pin14),
    .pin13(dipswitch_1_sw4[2]), .pin12(n7404_1_pin8), .pin11(n7408_6_pin11), .pin10(n7408_6_pin11),
    .pin9(dipswitch_1_sw4[0]), .pin8(n7408_6_pin8));
  _7408 #(.ShowInternalStructure("true"), .VccGndPorts("true")) u_7408_7 (
    .pin1(dipswitch_1_sw4[1]), .pin2(n7404_1_pin2), .pin3(n7408_7_pin3), .pin4(n7404_1_pin10),
    .pin5(n7404_1_pin2), .pin6(n7408_7_pin6), .pin7(n7404_1_pin7), .pin14(n7404_1_pin14),
    .pin13(dipswitch_1_sw4[3]), .pin12(dipswitch_1_sw4[1]), .pin11(n7408_7_pin11),
    .pin10(dipswitch_1_sw4[2]), .pin9(dipswitch_1_sw4[3]), .pin8(n7408_7_pin8));
  _7411 #(.ShowInternalStructure("true"), .VccGndPorts("true")) u_7411_3 (
    .pin1(dipswitch_1_sw4[2]), .pin2(n7404_1_pin8), .pin7(n7404_1_pin7), .pin14(n7404_1_pin14),
    .pin13(n7404_1_pin12), .pin12(n7411_3_pin12));  // open: pin3, pin4, pin5, pin6, pin11, pin10, pin9, pin8
  _7408 #(.ShowInternalStructure("true"), .VccGndPorts("true")) u_7408_8 (
    .pin1(n7404_1_pin10), .pin2(dipswitch_1_sw4[3]), .pin3(n7408_8_pin3), .pin4(dipswitch_1_sw4[3]),
    .pin5(dipswitch_1_sw4[1]), .pin6(n7408_8_pin6), .pin7(n7404_1_pin7), .pin14(n7404_1_pin14),
    .pin13(n7404_1_pin8), .pin12(n7404_1_pin2), .pin11(n7408_8_pin11), .pin10(dipswitch_1_sw4[2]),
    .pin9(n7404_1_pin2), .pin8(n7408_8_pin8));
  _7432 #(.ShowInternalStructure("true"), .VccGndPorts("true")) u_7432_2 (
    .pin1(n7408_1_pin11), .pin2(n7408_1_pin8), .pin3(n7432_2_pin3), .pin4(n7432_2_pin3), .pin5(n7408_1_pin6),
    .pin6(n7432_2_pin6), .pin7(n7404_1_pin7), .pin14(n7404_1_pin14), .pin13(n7411_1_pin6),
    .pin12(n7432_2_pin12), .pin11(n7432_2_pin11), .pin10(n7408_1_pin3), .pin9(n7432_2_pin6),
    .pin8(n7432_2_pin12));
  _7432 #(.ShowInternalStructure("true"), .VccGndPorts("true")) u_7432_3 (
    .pin1(n7432_3_pin1), .pin2(n7432_3_pin2), .pin3(n7432_3_pin3), .pin4(n7432_3_pin3), .pin5(n7432_3_pin5),
    .pin6(n7432_3_pin6), .pin7(n7404_1_pin7), .pin14(n7404_1_pin14), .pin13(dipswitch_1_sw4[2]),
    .pin12(n7404_1_pin8), .pin11(n7432_3_pin11), .pin10(n7432_3_pin11), .pin9(dipswitch_1_sw4[0]),
    .pin8(n7432_3_pin8));
  _7408 #(.ShowInternalStructure("true"), .VccGndPorts("true")) u_7408_9 (
    .pin1(n7404_1_pin12), .pin2(n7432_3_pin8), .pin3(n7432_3_pin5), .pin7(n7404_1_pin7),
    .pin14(n7404_1_pin14), .pin13(dipswitch_1_sw4[3]), .pin12(n7404_1_pin10), .pin11(n7432_3_pin1),
    .pin10(dipswitch_1_sw4[0]), .pin9(n7404_1_pin8), .pin8(n7432_3_pin2));  // open: pin4, pin5, pin6
  _7432 #(.ShowInternalStructure("true"), .VccGndPorts("true")) u_7432_4 (
    .pin1(n7411_1_pin12), .pin2(n7432_2_pin11), .pin3(n7432_4_pin3), .pin7(n7404_1_pin7),
    .pin14(n7404_1_pin14));  // open: pin4, pin5, pin6, pin13, pin12, pin11, pin10, pin9, pin8
  _7432 #(.ShowInternalStructure("true"), .VccGndPorts("true")) u_7432_5 (
    .pin1(n7408_2_pin8), .pin2(n7408_2_pin11), .pin3(n7432_5_pin3), .pin4(n7432_5_pin3), .pin5(n7411_2_pin6),
    .pin6(n7432_5_pin6), .pin7(n7404_1_pin7), .pin14(n7404_1_pin14), .pin13(n7411_2_pin8),
    .pin12(n7411_2_pin12), .pin11(n7432_5_pin11), .pin10(n7432_5_pin11), .pin9(n7432_5_pin6),
    .pin8(n7432_5_pin8));
  _7432 #(.ShowInternalStructure("true"), .VccGndPorts("true")) u_7432_6 (
    .pin1(n7408_7_pin6), .pin2(n7408_7_pin3), .pin3(n7432_6_pin3), .pin7(n7404_1_pin7),
    .pin14(n7404_1_pin14), .pin13(n7408_7_pin8), .pin12(n7408_7_pin11), .pin11(n7432_6_pin11),
    .pin10(n7432_6_pin11), .pin9(n7432_6_pin3), .pin8(n7432_6_pin8));  // open: pin4, pin5, pin6
  _7408 #(.ShowInternalStructure("true"), .VccGndPorts("true")) u_7408_10 (
    .pin1(dipswitch_1_sw4[1]), .pin2(n7404_1_pin10), .pin3(n7432_1_pin2), .pin7(n7404_1_pin7),
    .pin14(n7404_1_pin14));  // open: pin4, pin5, pin6, pin13, pin12, pin11, pin10, pin9, pin8
  _7432 #(.ShowInternalStructure("true"), .VccGndPorts("true")) u_7432_7 (
    .pin1(n7408_6_pin6), .pin2(n7408_3_pin11), .pin3(n7432_7_pin3), .pin4(n7432_7_pin3), .pin5(n7432_7_pin5),
    .pin6(n7432_7_pin6), .pin7(n7404_1_pin7), .pin14(n7404_1_pin14), .pin13(n7408_6_pin8),
    .pin12(n7408_5_pin6), .pin11(n7432_7_pin11), .pin10(n7432_7_pin11), .pin9(n7408_5_pin8),
    .pin8(n7432_7_pin5));
  _7432 #(.ShowInternalStructure("true"), .VccGndPorts("true")) u_7432_8 (
    .pin1(n7408_8_pin11), .pin2(n7408_8_pin8), .pin3(n7432_8_pin3), .pin4(n7432_8_pin3), .pin5(n7408_8_pin6),
    .pin6(n7432_8_pin6), .pin7(n7404_1_pin7), .pin14(n7404_1_pin14), .pin13(n7411_3_pin12),
    .pin12(n7408_8_pin3), .pin11(n7432_8_pin11), .pin10(n7432_8_pin11), .pin9(n7432_8_pin6),
    .pin8(n7432_8_pin8));
  _7_Segment_Display A (.a(n7432_4_pin3));  // open: g, f, b, e, d, c, dp
  _7_Segment_Display B (.b(n7432_5_pin8));  // open: g, f, a, e, d, c, dp
  _7_Segment_Display C (.c(n7432_3_pin6));  // open: g, f, a, b, e, d, dp
  _7432 #(.ShowInternalStructure("true"), .VccGndPorts("true")) u_7432_9 (
    .pin7(n7404_1_pin7), .pin14(n7404_1_pin14), .pin13(n7432_1_pin6), .pin12(n7408_4_pin11),
    .pin11(n7432_9_pin11));  // open: pin1, pin2, pin3, pin4, pin5, pin6, pin10, pin9, pin8
  _7_Segment_Display D (.d(n7432_7_pin6));  // open: g, f, a, b, e, c, dp
  _7_Segment_Display E (.e(n7432_6_pin8));  // open: g, f, a, b, d, c, dp
  _7_Segment_Display F (.f(n7432_8_pin8));  // open: g, a, b, e, d, c, dp
  _7_Segment_Display G (.g(n7432_9_pin11));  // open: f, a, b, e, d, c, dp
  _7_Segment_Display u_7_segment_display_1 (
    .g(n7432_9_pin11), .f(n7432_8_pin8), .a(n7432_4_pin3), .b(n7432_5_pin8), .e(n7432_6_pin8),
    .d(n7432_7_pin6), .c(n7432_3_pin6));  // open: dp
  // also tied to GND on the sheet: n7404_1_pin7
  // also tied to VCC on the sheet: n7404_1_pin14
endmodule
