// Logisim project BinToHex.circ as structural Verilog: 1 circuit, main circuit main
module main (
  input  in_1
);

  wire and_1_out, and_2_out, clock_1_out;
  wire [3:0] t_ff_1_q;
  wire [6:0] rom_1_data;

  ROM #(.addrWidth(4), .dataWidth(7)) rom_1 (.addr(t_ff_1_q), .data(rom_1_data));
  _7_Segment_Display u_7_segment_display_1 (
    .g(rom_1_data[0]), .f(rom_1_data[1]), .a(rom_1_data[6]), .b(rom_1_data[5]), .e(rom_1_data[2]),
    .d(rom_1_data[3]), .c(rom_1_data[4]));  // open: dp
  T_Flip_Flop t_ff_1 (.T(in_1), .clk(clock_1_out), .Q(t_ff_1_q[0]));  // open: Qn, reset, preset
  Clock clock_1 (.out(clock_1_out));
  T_Flip_Flop t_ff_2 (.T(t_ff_1_q[0]), .clk(clock_1_out), .Q(t_ff_1_q[1]));  // open: Qn, reset, preset
  T_Flip_Flop t_ff_3 (.T(and_1_out), .clk(clock_1_out), .Q(t_ff_1_q[2]));  // open: Qn, reset, preset
  and and_1 (and_1_out, t_ff_1_q[0], t_ff_1_q[1]);
  T_Flip_Flop t_ff_4 (.T(and_2_out), .clk(clock_1_out), .Q(t_ff_1_q[3]));  // open: Qn, reset, preset
  and and_2 (and_2_out, and_1_out, t_ff_1_q[2]);

  // Notes on the sheet:
  //   contents of rom_1 (hex, n*v repeats v):
  //   7e 30 6d 79 33 5b 5f 70 7f 7b 77 1f 4e 3d 4f 47
endmodule
